// Digital circuit DEMUX-1-4.dig as structural Verilog
module DEMUX_1_4 (
  input  Din,
  input  S1,
  input  S0,
  output Output1,
  output Output2,
  output Output3,
  output Output4
);

  wire not_1_out, not_2_out, not_3_out, not_4_out;

  not not_1 (not_1_out, S0);
  not not_2 (not_2_out, S1);
  not not_3 (not_3_out, S0);
  not not_4 (not_4_out, S1);
  and and_1 (Output1, Din, not_1_out, not_2_out);
  and and_2 (Output2, Din, not_3_out, S1);
  and and_3 (Output3, Din, S0, not_4_out);
  and and_4 (Output4, Din, S0, S1);
endmodule
