// Digital circuit Flip-Flop-JK.dig as structural Verilog
module Flip_Flop_JK (
  input  K,
  input  J,
  input  Clock,
  input  J_2,
  input  Clock_2,
  input  K_2,
  output Q,
  output Q_2,
  output q_3,
  output q_4
);

  wire nand_1_out, nand_2_out, nand_5_out, nand_6_out, nand_7_out, nand_8_out, nand_9_out, nand_10_out,
       not_1_out;

  nand nand_1 (nand_1_out, q_4, J_2, Clock_2);
  nand nand_2 (nand_2_out, Clock_2, K_2, q_3);
  nand nand_3 (q_3, nand_1_out, q_4);
  nand nand_4 (q_4, q_3, nand_2_out);
  nand nand_5 (nand_5_out, Q_2, J, Clock);
  nand nand_6 (nand_6_out, Clock, K, Q);
  nand nand_7 (nand_7_out, nand_5_out, nand_8_out);
  nand nand_8 (nand_8_out, nand_7_out, nand_6_out);
  not not_1 (not_1_out, Clock);
  nand nand_9 (nand_9_out, nand_7_out, not_1_out);
  nand nand_10 (nand_10_out, not_1_out, nand_8_out);
  nand nand_11 (Q, nand_9_out, Q_2);
  nand nand_12 (Q_2, Q, nand_10_out);

  // Notes on the sheet:
  //   Flip Flop JK simplificada.
  //   Este flip flop presenta problemas que surgen con el tiempo. El pulso del clock debe ser muy corto porque un cambio en 'q'
  //   antes de que el clock se apague y al tener J y K encendidas, hace conducir el circuito a una oscilación indeterminada. Por otra parte al tener el Clock activo
  //   y alguna de las entradas activas se produce un cambio a la salida. Las compuertas NAND de la primera parte hace las salidas sean totalmente
  //   excluyentes.
  //   Flip Flop JK máster-slave.
  //   Para corregir el problema de la oscilación indeterminada (también llamado carrera) se desarrolló el flip flop máster-slave
  //   que proporciona mayor estabilidad. TIene dos flip flops JK atados juntos, con el segundo impulsado por una señal de clock de
  //   manera invertida. El circuito máster es el encargado de dar las condiciones que se deben guardar, mientras que el circuito slave
  //   las recibe después de tener apagado el Clock, generando un retraso. Cuando el Clock está encendido el máster se actualiza y
  //   en el caso contrario se actualiza el slave. Este funcionamiento permite corregir el problema de la "carrera".
endmodule
