// Digital circuit Flip-Flops-RS.dig as structural Verilog
module Flip_Flops_RS (
  input  Set,
  input  Reset,
  input  Clock,
  input  Set_2,
  input  Clock_2,
  input  Reset_2,
  input  S,
  input  R,
  input  C,
  output Q,
  output Q_2,
  output Output,
  output q_3,
  output q_4
);

  wire nand_1_out, nand_2_out, nand_3_out, nand_4_out, nand_5_out, nand_6_out, nand_9_out, nand_10_out,
       not_1_out;

  nand nand_1 (nand_1_out, S, C);
  nand nand_2 (nand_2_out, C, R);
  nand nand_3 (nand_3_out, nand_1_out, nand_4_out);
  nand nand_4 (nand_4_out, nand_3_out, nand_2_out);
  not not_1 (not_1_out, C);
  nand nand_5 (nand_5_out, nand_3_out, not_1_out);
  nand nand_6 (nand_6_out, not_1_out, nand_4_out);
  nand nand_7 (q_3, nand_5_out, q_4);
  nand nand_8 (q_4, q_3, nand_6_out);
  nand nand_9 (nand_9_out, Set, Clock);
  nand nand_10 (nand_10_out, Clock, Reset);
  RS_FF rs_ff_1 (.S(Set_2), .C(Clock_2), .R(Reset_2), .Q(Output));  // open: nQ
  nand nand_11 (Q, nand_9_out, Q_2);
  nand nand_12 (Q_2, Q, nand_10_out);

  // Notes on the sheet:
  //   Flip Flop RS maestro-esclavo.
  //   El circuito representa dos sistemas biestables, donde la entrada de reloj se utiliza para habilitar cada uno.
  //   El funcionamiento consiste en que cuando la señal de entrada de reloj pasa a nivel alto, se habilita el maestro y se
  //   deshabilita el esclavo. El maestro se comporta como un latch con entrada de habilitación R-S ,
  //   y el esclavo permanece inhabilitado, entonces las salidas no cambian.Cuando el reloj se hace ‘0’, 
  //   el maestro se deshabilita y mantiene su estado previo y el esclavo se habilita y responde a sus entradas. 
  //   Como la salida Q’ del maestro está conectada a la entrada S’ del esclavo y la salida 'Q del maestro está 
  //   conectada a la entrada R´ del esclavo, este siempre verá un ‘1’ en una entrada y un ‘0’ en la otra. Si la salida Q del
  //   maestro es ‘1’, el esclavo estará en el estado SET y si es ‘0’, estará en el estado RESET. Por
  //   tanto, cuando el esclavo está habilitado toma el estado de salida del maestro.
  //   Q´
  //   Q
  //   S´
  //   R´
  //   En ambos circuitos se presenta una oscilación indeterminada al tener el 'Set 'y el 'Reset' en 1 (encendido), ocasionando que el sistema oscile como respuesta de salida entre 0 y 1 a la vez, 
  //   sin determinar el estado de salida del sistema. SIn embargo, sin el uso de compuertas lógicas sino de flexores este problema puede ser solucionado.
  //   Los Flip-Flops RS son dispositivos síncronos. Cuando un pulso de reloj llega al Clock, con ambas entradas en 0 (R y S), las salidas no cambian. 
  //   El siguiente estado se da cuando la salida normal Q se borra debido aun nivel alto en R y la activación de un pulso de reloj para la entrada Clock.
  //   Para el caso en el que R=1 y S=0 el Flip Flop no se va a 0 inmediatamente sino que se debe esperar a que el pulso de reloj pase de un nivel bajo a uno alto.
  //   Si se tiene un nivel alto activo en la entrada S y con R=0 y el pulso de reloj en un nivel alto, se lleva la salida Q a 1. Sin embargo, cuando ambas entradas están
  //   en 1, el sistema comienza a oscilar y el programa nos muestra un error.
endmodule
