// Digital circuit MUX-8-1.dig as structural Verilog
module MUX_8_1 (
  input  D7,
  input  D6,
  input  D5,
  input  D4,
  input  D3,
  input  D2,
  input  D1,
  input  D0,
  input  Sel0,
  input  Sel1,
  input  Sel2,
  output Output
);

  wire and_1_out, and_2_out, and_3_out, and_4_out, and_5_out, and_6_out, and_7_out, and_8_out, not_1_out,
       not_2_out, not_3_out;

  not not_1 (not_1_out, Sel0);
  not not_2 (not_2_out, Sel1);
  not not_3 (not_3_out, Sel2);
  and and_1 (and_1_out, D7, not_1_out, not_2_out, not_3_out);
  and and_2 (and_2_out, D6, not_3_out, not_2_out, Sel0);
  and and_3 (and_3_out, D5, not_3_out, not_1_out, Sel1);
  and and_4 (and_4_out, D4, not_3_out, Sel1, Sel0);
  and and_5 (and_5_out, D3, not_1_out, Sel1, Sel2);
  or or_1 (Output, and_8_out, and_7_out, and_6_out, and_5_out, and_4_out, and_3_out, and_2_out, and_1_out);
  and and_6 (and_6_out, D2, Sel0, not_2_out, Sel2);
  and and_7 (and_7_out, D1, not_1_out, Sel1, Sel2);
  and and_8 (and_8_out, D0, Sel0, Sel1, Sel2);
endmodule
