// Digital circuit pin.dig as structural Verilog
module pin (
  input  Clear,
  input  Enable,
  input  Set,
  input  Clear_2,
  input  Enable_2,
  input  Set_2,
  input  Clear_3,
  input  Enable_3,
  input  Set_3,
  input  in_10,
  input  Ci0,
  input  Ci1,
  input  Ci2,
  input  Ci3,
  input  Si0,
  input  Si1,
  input  Si2,
  input  Si3,
  input  in_24,
  input  in_26,
  input  in_28,
  input  Clock,
  input  Clock_2,
  input  Clock_3,
  output out_11,
  output out_16,
  output out_17,
  output out_18,
  output out_19,
  output out_25,
  output out_27,
  output out_29
);

  wire d_ff_as_1_q, d_ff_as_4_q, d_ff_as_7_q, d_ff_as_10_q, in0, in1, in2, in3, multiplexer_1_out,
       multiplexer_2_out, multiplexer_3_out, multiplexer_4_out, multiplexer_5_out, multiplexer_6_out,
       multiplexer_7_out, multiplexer_8_out, multiplexer_9_out, multiplexer_10_out, multiplexer_11_out,
       multiplexer_12_out, Out0, Out1, Out2, Out3;

  Multiplexer multiplexer_1 (.sel(Enable), .in_0(d_ff_as_1_q), .in_1(Ci0), .out(multiplexer_1_out));
  PullDown pulldown_1 (.out(in0));
  Multiplexer multiplexer_2 (.sel(Enable_2), .in_0(out_16), .in_1(in0), .out(multiplexer_2_out));
  Multiplexer multiplexer_3 (.sel(Enable_3), .in_0(Out0), .in_1(Si0), .out(multiplexer_3_out));
  D_FF_AS d_ff_as_1 (.Set(Set), .D(multiplexer_1_out), .C(Clock), .Clr(Clear), .Q(d_ff_as_1_q));  // open: nQ
  assign out_11 = ~d_ff_as_1_q ? Out0 : 1'bz;  // DriverInvSel driverinvsel_1
  D_FF_AS d_ff_as_2 (.Set(Set_2), .D(multiplexer_2_out), .C(Clock_2), .Clr(Clear_2), .Q(out_16));  // open: nQ
  D_FF_AS d_ff_as_3 (.Set(Set_3), .D(multiplexer_3_out), .C(Clock_3), .Clr(Clear_3), .Q(Out0));  // open: nQ
  assign in0 = d_ff_as_1_q ? in_10 : 1'bz;  // Driver driver_1
  Multiplexer multiplexer_4 (.sel(Enable), .in_0(d_ff_as_4_q), .in_1(Ci1), .out(multiplexer_4_out));
  PullDown pulldown_2 (.out(in1));
  D_FF_AS d_ff_as_4 (.Set(Set), .D(multiplexer_4_out), .C(Clock), .Clr(Clear), .Q(d_ff_as_4_q));  // open: nQ
  Multiplexer multiplexer_5 (.sel(Enable_2), .in_0(out_17), .in_1(in1), .out(multiplexer_5_out));
  Multiplexer multiplexer_6 (.sel(Enable_3), .in_0(Out1), .in_1(Si1), .out(multiplexer_6_out));
  assign out_25 = ~d_ff_as_4_q ? Out1 : 1'bz;  // DriverInvSel driverinvsel_2
  D_FF_AS d_ff_as_5 (.Set(Set_2), .D(multiplexer_5_out), .C(Clock_2), .Clr(Clear_2), .Q(out_17));  // open: nQ
  D_FF_AS d_ff_as_6 (.Set(Set_3), .D(multiplexer_6_out), .C(Clock_3), .Clr(Clear_3), .Q(Out1));  // open: nQ
  assign in1 = d_ff_as_4_q ? in_24 : 1'bz;  // Driver driver_2
  Multiplexer multiplexer_7 (.sel(Enable), .in_0(d_ff_as_7_q), .in_1(Ci2), .out(multiplexer_7_out));
  PullDown pulldown_3 (.out(in2));
  D_FF_AS d_ff_as_7 (.Set(Set), .D(multiplexer_7_out), .C(Clock), .Clr(Clear), .Q(d_ff_as_7_q));  // open: nQ
  Multiplexer multiplexer_8 (.sel(Enable_2), .in_0(out_18), .in_1(in2), .out(multiplexer_8_out));
  Multiplexer multiplexer_9 (.sel(Enable_3), .in_0(Out2), .in_1(Si2), .out(multiplexer_9_out));
  assign out_27 = ~d_ff_as_7_q ? Out2 : 1'bz;  // DriverInvSel driverinvsel_3
  D_FF_AS d_ff_as_8 (.Set(Set_2), .D(multiplexer_8_out), .C(Clock_2), .Clr(Clear_2), .Q(out_18));  // open: nQ
  D_FF_AS d_ff_as_9 (.Set(Set_3), .D(multiplexer_9_out), .C(Clock_3), .Clr(Clear_3), .Q(Out2));  // open: nQ
  assign in2 = d_ff_as_7_q ? in_26 : 1'bz;  // Driver driver_3
  Multiplexer multiplexer_10 (.sel(Enable), .in_0(d_ff_as_10_q), .in_1(Ci3), .out(multiplexer_10_out));
  PullDown pulldown_4 (.out(in3));
  D_FF_AS d_ff_as_10 (.Set(Set), .D(multiplexer_10_out), .C(Clock), .Clr(Clear), .Q(d_ff_as_10_q));  // open: nQ
  Multiplexer multiplexer_11 (.sel(Enable_2), .in_0(out_19), .in_1(in3), .out(multiplexer_11_out));
  Multiplexer multiplexer_12 (.sel(Enable_3), .in_0(Out3), .in_1(Si3), .out(multiplexer_12_out));
  assign out_29 = ~d_ff_as_10_q ? Out3 : 1'bz;  // DriverInvSel driverinvsel_4
  D_FF_AS d_ff_as_11 (.Set(Set_2), .D(multiplexer_11_out), .C(Clock_2), .Clr(Clear_2), .Q(out_19));  // open: nQ
  D_FF_AS d_ff_as_12 (.Set(Set_3), .D(multiplexer_12_out), .C(Clock_3), .Clr(Clear_3), .Q(Out3));  // open: nQ
  assign in3 = d_ff_as_10_q ? in_28 : 1'bz;  // Driver driver_4

  // Notes on the sheet:
  //   A continuación se muestra el primer registro encargado del comportamiento
  //   del pin (controla la dirección del pin).
  //   El segundo resgistro corresponde a la configuración de entrada. Este es el encargado de almacenar el estado del pin.
  //   Por último, se tiene el tercer registro, el cual controla el estado del pin, si éste ha sido configurado como una salida.
  //   Para el registro de configuración se toma como:
  //   1- Entrada
  //   0-Salida
  //   Se utilizaron dos buffer tri-state encargados de conectar el pin con el
  //   registro de almacenamiento o con el registro de salida. Los buffer tri-state
  //   están conectados de manera mutuamente excluyente. El paso de información 
  //   es controlado por el enable, presente en cada uno de los registros.
  //   Se utilizaron resistencias pull-down para el registro de almacenamiento, con el
  //   fin que el pin de entrada envíe el dato y se transforme esa alta impedancia en 
  //   un 0 lógico.
endmodule
